// Logisim project KBCPU.circ as structural Verilog: 12 circuits, main circuit main
module main (
  input  [7:0] in_1,
  input  in_2,
  input  in_3,
  input  in_4,
  input  [7:0] in_5,
  input  in_6,
  input  [7:0] in_7,
  input  [7:0] in_8,
  input  [7:0] in_9,
  output [7:0] out_10,
  output out_11,
  output [7:0] out_12,
  output out_13,
  output [7:0] out_14,
  output out_15
);

  R_8 A (.INPUT_8(in_1), .WE(in_2), .OUTPUT_8(out_10));
  R_1 r_1_1 (.INPUT_1(in_3), .WE(in_4), .Q(out_11));  // open: out_3
  ALU_ADDSUB alu_addsub_1 (.SUB(in_6), .INPUT_1(in_5), .INPUT_2(in_7), .Cout(out_13), .OUTPUT_1(out_12));
  ALU_ADDER_8B alu_adder_8b_1 (.INPUT_1(in_8), .INPUT_2(in_9), .OUTPUT_1(out_14), .Cout(out_15));
endmodule

module G_XOR (
  input  in_1,
  input  in_2,
  output out_3
);

  wire and_1_out, and_2_out, not_1_out, not_2_out;

  not not_1 (not_1_out, in_2);
  not not_2 (not_2_out, in_1);
  and and_1 (and_1_out, in_1, not_1_out);
  and and_2 (and_2_out, not_2_out, in_2);
  or or_1 (out_3, and_1_out, and_2_out);
endmodule

module ALU_ADDER_HALF (
  input  INPUT_1,
  input  INPUT_2,
  output SUM,
  output Cout
);

  xor xor_1 (SUM, INPUT_1, INPUT_2);
  and and_1 (Cout, INPUT_1, INPUT_2);
endmodule

module ALU_ADDER_FULL (
  input  INPUT_1,
  input  INPUT_2,
  input  Cin,
  output SUM,
  output Cout
);

  wire alu_adder_half_1_cout, alu_adder_half_1_sum, alu_adder_half_2_cout;

  ALU_ADDER_HALF alu_adder_half_1 (
    .INPUT_1(INPUT_1), .INPUT_2(INPUT_2), .SUM(alu_adder_half_1_sum), .Cout(alu_adder_half_1_cout));
  ALU_ADDER_HALF alu_adder_half_2 (
    .INPUT_1(alu_adder_half_1_sum), .INPUT_2(Cin), .SUM(SUM), .Cout(alu_adder_half_2_cout));
  or or_1 (Cout, alu_adder_half_2_cout, alu_adder_half_1_cout);
endmodule

module ALU_ADDER_8 (
  input  INPUT1_3,
  input  INPUT1_4,
  input  INPUT1_5,
  input  INPUT1_6,
  input  INPUT1_7,
  input  INPUT1_8,
  input  INPUT1_2,
  input  INPUT2_3,
  input  INPUT2_4,
  input  INPUT2_5,
  input  INPUT2_6,
  input  INPUT2_7,
  input  INPUT2_8,
  input  INPUT2_2,
  input  INPUT1_1,
  input  INPUT2_1,
  output OUTPUT_2,
  output OUTPUT_3,
  output OUTPUT_4,
  output OUTPUT_5,
  output OUTPUT_6,
  output OUTPUT_7,
  output OUTPUT_1,
  output OUTPUT_8,
  output Cout
);

  wire FULL1_cout, FULL2_cout, FULL3_cout, FULL4_cout, FULL5_cout, FULL6_cout, HALF1_cout;

  ALU_ADDER_HALF HALF1 (.INPUT_1(INPUT1_1), .INPUT_2(INPUT2_1), .SUM(OUTPUT_1), .Cout(HALF1_cout));
  ALU_ADDER_FULL FULL1 (.INPUT_1(INPUT1_2), .INPUT_2(INPUT2_2), .Cin(HALF1_cout), .SUM(OUTPUT_2), .Cout(FULL1_cout));
  ALU_ADDER_FULL FULL2 (.INPUT_1(INPUT1_3), .INPUT_2(INPUT2_3), .Cin(FULL1_cout), .SUM(OUTPUT_3), .Cout(FULL2_cout));
  ALU_ADDER_FULL FULL3 (.INPUT_1(INPUT1_4), .INPUT_2(INPUT2_4), .Cin(FULL2_cout), .SUM(OUTPUT_4), .Cout(FULL3_cout));
  ALU_ADDER_FULL FULL4 (.INPUT_1(INPUT1_5), .INPUT_2(INPUT2_5), .Cin(FULL3_cout), .SUM(OUTPUT_5), .Cout(FULL4_cout));
  ALU_ADDER_FULL FULL5 (.INPUT_1(INPUT1_6), .INPUT_2(INPUT2_6), .Cin(FULL4_cout), .SUM(OUTPUT_6), .Cout(FULL5_cout));
  ALU_ADDER_FULL FULL6 (.INPUT_1(INPUT1_7), .INPUT_2(INPUT2_7), .Cin(FULL5_cout), .SUM(OUTPUT_7), .Cout(FULL6_cout));
  ALU_ADDER_FULL FULL7 (.INPUT_1(INPUT1_8), .INPUT_2(INPUT2_8), .Cin(FULL6_cout), .SUM(OUTPUT_8), .Cout(Cout));
endmodule

module ALU_ADDER_8B (
  input  [7:0] INPUT_1,
  input  [7:0] INPUT_2,
  output [7:0] OUTPUT_1,
  output Cout
);

  wire FULL1_cout, FULL2_cout, FULL3_cout, FULL4_cout, FULL5_cout, FULL6_cout, HALF1_cout;

  ALU_ADDER_HALF HALF1 (.INPUT_1(INPUT_1[0]), .INPUT_2(INPUT_2[0]), .SUM(OUTPUT_1[0]), .Cout(HALF1_cout));
  ALU_ADDER_FULL FULL1 (
    .INPUT_1(INPUT_1[1]), .INPUT_2(INPUT_2[1]), .Cin(HALF1_cout), .SUM(OUTPUT_1[1]), .Cout(FULL1_cout));
  ALU_ADDER_FULL FULL2 (
    .INPUT_1(INPUT_1[2]), .INPUT_2(INPUT_2[2]), .Cin(FULL1_cout), .SUM(OUTPUT_1[2]), .Cout(FULL2_cout));
  ALU_ADDER_FULL FULL3 (
    .INPUT_1(INPUT_1[3]), .INPUT_2(INPUT_2[3]), .Cin(FULL2_cout), .SUM(OUTPUT_1[3]), .Cout(FULL3_cout));
  ALU_ADDER_FULL FULL4 (
    .INPUT_1(INPUT_1[4]), .INPUT_2(INPUT_2[4]), .Cin(FULL3_cout), .SUM(OUTPUT_1[4]), .Cout(FULL4_cout));
  ALU_ADDER_FULL FULL5 (
    .INPUT_1(INPUT_1[5]), .INPUT_2(INPUT_2[5]), .Cin(FULL4_cout), .SUM(OUTPUT_1[5]), .Cout(FULL5_cout));
  ALU_ADDER_FULL FULL6 (
    .INPUT_1(INPUT_1[6]), .INPUT_2(INPUT_2[6]), .Cin(FULL5_cout), .SUM(OUTPUT_1[6]), .Cout(FULL6_cout));
  ALU_ADDER_FULL FULL7 (.INPUT_1(INPUT_1[7]), .INPUT_2(INPUT_2[7]), .Cin(FULL6_cout), .SUM(OUTPUT_1[7]), .Cout(Cout));
endmodule

module ALU_SUB_HALF (
  input  INPUT_1,
  input  INPUT_2,
  output DIFF,
  output Bout
);

  wire not_1_out;

  not not_1 (not_1_out, INPUT_1);
  xor xor_1 (DIFF, INPUT_1, INPUT_2);
  and and_1 (Bout, INPUT_2, not_1_out);
endmodule

module ALU_SUB_FULL (
  input  INPUT_1,
  input  INPUT_2,
  input  Bin,
  output DIFF,
  output Bout
);

  wire alu_sub_half_1_bout, alu_sub_half_1_diff, alu_sub_half_2_bout;

  ALU_SUB_HALF alu_sub_half_1 (
    .INPUT_1(INPUT_1), .INPUT_2(INPUT_2), .DIFF(alu_sub_half_1_diff), .Bout(alu_sub_half_1_bout));
  ALU_SUB_HALF alu_sub_half_2 (.INPUT_1(alu_sub_half_1_diff), .INPUT_2(Bin), .DIFF(DIFF), .Bout(alu_sub_half_2_bout));
  or or_1 (Bout, alu_sub_half_2_bout, alu_sub_half_1_bout);
endmodule

module ALU_ADDSUB (
  input  [7:0] INPUT_2,
  input  SUB,
  input  [7:0] INPUT_1,
  output [7:0] OUTPUT_1,
  output Cout
);

  wire alu_adder_full_1_cout, FULL1_cout, FULL2_cout, FULL3_cout, FULL4_cout, FULL5_cout, FULL6_cout,
       xor_1_out, xor_2_out, xor_3_out, xor_4_out, xor_5_out, xor_6_out, xor_7_out, xor_8_out;

  xor xor_1 (xor_1_out, INPUT_2[0], SUB);
  xor xor_2 (xor_2_out, INPUT_2[1], SUB);
  xor xor_3 (xor_3_out, INPUT_2[2], SUB);
  xor xor_4 (xor_4_out, INPUT_2[3], SUB);
  xor xor_5 (xor_5_out, INPUT_2[4], SUB);
  xor xor_6 (xor_6_out, INPUT_2[5], SUB);
  ALU_ADDER_FULL alu_adder_full_1 (
    .INPUT_1(xor_1_out), .INPUT_2(INPUT_1[0]), .Cin(SUB), .SUM(OUTPUT_1[0]), .Cout(alu_adder_full_1_cout));
  xor xor_7 (xor_7_out, INPUT_2[6], SUB);
  xor xor_8 (xor_8_out, INPUT_2[7], SUB);
  ALU_ADDER_FULL FULL1 (
    .INPUT_1(xor_2_out), .INPUT_2(INPUT_1[1]), .Cin(alu_adder_full_1_cout), .SUM(OUTPUT_1[1]),
    .Cout(FULL1_cout));
  ALU_ADDER_FULL FULL2 (
    .INPUT_1(xor_3_out), .INPUT_2(INPUT_1[2]), .Cin(FULL1_cout), .SUM(OUTPUT_1[2]), .Cout(FULL2_cout));
  ALU_ADDER_FULL FULL3 (
    .INPUT_1(xor_4_out), .INPUT_2(INPUT_1[3]), .Cin(FULL2_cout), .SUM(OUTPUT_1[3]), .Cout(FULL3_cout));
  ALU_ADDER_FULL FULL4 (
    .INPUT_1(xor_5_out), .INPUT_2(INPUT_1[4]), .Cin(FULL3_cout), .SUM(OUTPUT_1[4]), .Cout(FULL4_cout));
  ALU_ADDER_FULL FULL5 (
    .INPUT_1(xor_6_out), .INPUT_2(INPUT_1[5]), .Cin(FULL4_cout), .SUM(OUTPUT_1[5]), .Cout(FULL5_cout));
  ALU_ADDER_FULL FULL6 (
    .INPUT_1(xor_7_out), .INPUT_2(INPUT_1[6]), .Cin(FULL5_cout), .SUM(OUTPUT_1[6]), .Cout(FULL6_cout));
  ALU_ADDER_FULL FULL7 (.INPUT_1(xor_8_out), .INPUT_2(INPUT_1[7]), .Cin(FULL6_cout), .SUM(OUTPUT_1[7]), .Cout(Cout));
endmodule

module R_1 (
  input  INPUT_1,
  input  WE,
  output out_3,
  output Q
);

  wire and_1_out, and_2_out, not_1_out;

  not not_1 (not_1_out, INPUT_1);
  and and_1 (and_1_out, INPUT_1, WE);
  and and_2 (and_2_out, WE, not_1_out);
  nor nor_1 (out_3, and_1_out, Q);
  nor nor_2 (Q, out_3, and_2_out);
endmodule

module R_8 (
  input  [7:0] INPUT_8,
  input  WE,
  output [7:0] OUTPUT_8
);

  R_1 r_1_1 (.INPUT_1(INPUT_8[7]), .WE(WE), .Q(OUTPUT_8[7]));  // open: out_3
  R_1 r_1_2 (.INPUT_1(INPUT_8[6]), .WE(WE), .Q(OUTPUT_8[6]));  // open: out_3
  R_1 r_1_3 (.INPUT_1(INPUT_8[5]), .WE(WE), .Q(OUTPUT_8[5]));  // open: out_3
  R_1 r_1_4 (.INPUT_1(INPUT_8[4]), .WE(WE), .Q(OUTPUT_8[4]));  // open: out_3
  R_1 r_1_5 (.INPUT_1(INPUT_8[3]), .WE(WE), .Q(OUTPUT_8[3]));  // open: out_3
  R_1 r_1_6 (.INPUT_1(INPUT_8[2]), .WE(WE), .Q(OUTPUT_8[2]));  // open: out_3
  R_1 r_1_7 (.INPUT_1(INPUT_8[1]), .WE(WE), .Q(OUTPUT_8[1]));  // open: out_3
  R_1 r_1_8 (.INPUT_1(INPUT_8[0]), .WE(WE), .Q(OUTPUT_8[0]));  // open: out_3
endmodule

module R_16 (
  input  [15:0] INPUT_8,
  input  WE,
  output [15:0] OUTPUT_8
);

  R_1 r_1_1 (.INPUT_1(INPUT_8[15]), .WE(WE), .Q(OUTPUT_8[15]));  // open: out_3
  R_1 r_1_2 (.INPUT_1(INPUT_8[14]), .WE(WE), .Q(OUTPUT_8[14]));  // open: out_3
  R_1 r_1_3 (.INPUT_1(INPUT_8[13]), .WE(WE), .Q(OUTPUT_8[13]));  // open: out_3
  R_1 r_1_4 (.INPUT_1(INPUT_8[12]), .WE(WE), .Q(OUTPUT_8[12]));  // open: out_3
  R_1 r_1_5 (.INPUT_1(INPUT_8[11]), .WE(WE), .Q(OUTPUT_8[11]));  // open: out_3
  R_1 r_1_6 (.INPUT_1(INPUT_8[10]), .WE(WE), .Q(OUTPUT_8[10]));  // open: out_3
  R_1 r_1_7 (.INPUT_1(INPUT_8[9]), .WE(WE), .Q(OUTPUT_8[9]));  // open: out_3
  R_1 r_1_8 (.INPUT_1(INPUT_8[8]), .WE(WE), .Q(OUTPUT_8[8]));  // open: out_3
  R_1 r_1_9 (.INPUT_1(INPUT_8[7]), .WE(WE), .Q(OUTPUT_8[7]));  // open: out_3
  R_1 r_1_10 (.INPUT_1(INPUT_8[6]), .WE(WE), .Q(OUTPUT_8[6]));  // open: out_3
  R_1 r_1_11 (.INPUT_1(INPUT_8[5]), .WE(WE), .Q(OUTPUT_8[5]));  // open: out_3
  R_1 r_1_12 (.INPUT_1(INPUT_8[4]), .WE(WE), .Q(OUTPUT_8[4]));  // open: out_3
  R_1 r_1_13 (.INPUT_1(INPUT_8[3]), .WE(WE), .Q(OUTPUT_8[3]));  // open: out_3
  R_1 r_1_14 (.INPUT_1(INPUT_8[2]), .WE(WE), .Q(OUTPUT_8[2]));  // open: out_3
  R_1 r_1_15 (.INPUT_1(INPUT_8[1]), .WE(WE), .Q(OUTPUT_8[1]));  // open: out_3
  R_1 r_1_16 (.INPUT_1(INPUT_8[0]), .WE(WE), .Q(OUTPUT_8[0]));  // open: out_3
endmodule
